# Fritzing sketch full_bridge (saved by Fritzing 0.9.4)
breadboards: 1

parts:
  J1 = LOAD_CELL [package=1x03]
  J2 = LOAD_CELL [package=1x03]
  J3 = LOAD_CELL [package=1x03]
  J4 = LOAD_CELL [package=1x03]
  part = HX711 Weighing Sensor Module
  part_2 = Photon

nets:
  N1: J1.B, J2.B, part.E+
  N2: J1.R, J3.R, part.A-
  N3: J2.R, J4.R, part.A+
  N4: J3.B, J4.B, part.E-
  VCC: part.VCC, part_2.VIN
  GND: part.GND, part_2.GND
  N5: part.DO/RX, part_2.D3
  N6: part.CK/TX, part_2.D2
